# Fritzing sketch lab5 (saved by Fritzing 0.9.1b)
breadboards: 4

parts:
  Part1 = Arduino Nano (Rev3.0)
  T1 = LM35 Temperature Sensor [package="TO92 [THT]"]
  U2 = HC-SR04 [chip_label=IC package="SIP (Single Inline) [THT]"]
  C2 = Capacitor Polarized [package=cpol-radial-100uf-25v]  # not connected
  M1 = Stepper Motor - Bipolar  # not connected
  A4988 = Motor Driver 1A Dual TB6612FNG [part_number=A4988]  # not connected

nets:
  GND: Part1.GND, T1.GND, U2.GND
  N1: Part1.D7, U2.Trig
  N2: Part1.D8, U2.Echo
  5V: Part1.5V, T1.+Vs, U2.Vcc
  N3: Part1.A0, T1.Vout

notes:
  These power and ground wires connect to external 12V source used needed by stepper motor.

custom parts:
  HC-SR04: HC-SR04 ultrasound distance sensor
